// Logisim project Control_Unit.circ as structural Verilog: 1 circuit, main circuit main
module main (
  input  in_1,
  input  in_2,
  input  in_3,
  input  in_4,
  output out_5,
  output out_6,
  output out_7,
  output out_8,
  output out_9,
  output out_10
);

  wire and_1_out, and_2_out, and_3_out, and_4_out, and_5_out, and_6_out, and_8_out, and_9_out, d_ff_1_qn,
       d_ff_2_q, d_ff_3_q, not_1_out, not_2_out, or_1_out, or_2_out;

  and and_1 (and_1_out, out_10, out_5, out_6);
  and and_2 (and_2_out, d_ff_1_qn, out_5, d_ff_3_q, in_3);
  and and_3 (and_3_out, d_ff_1_qn, out_5, d_ff_3_q, not_1_out);
  and and_4 (and_4_out, d_ff_1_qn, out_6);
  and and_5 (and_5_out, d_ff_1_qn, not_1_out, not_2_out);
  and and_6 (and_6_out, d_ff_1_qn, d_ff_2_q);
  not not_1 (not_1_out, in_3);
  not not_2 (not_2_out, in_4);
  or or_1 (or_1_out, and_1_out, and_2_out);
  or or_2 (or_2_out, and_4_out, and_5_out, and_6_out);
  D_Flip_Flop d_ff_1 (.D(or_1_out), .clk(in_1), .Q(out_10), .Qn(d_ff_1_qn), .reset(in_2));  // open: preset
  D_Flip_Flop d_ff_2 (.D(and_3_out), .clk(in_1), .Q(d_ff_2_q), .Qn(out_5), .reset(in_2));  // open: preset
  D_Flip_Flop d_ff_3 (.D(or_2_out), .clk(in_1), .Q(d_ff_3_q), .Qn(out_6), .reset(in_2));  // open: preset
  and and_7 (out_7, d_ff_1_qn, out_6);
  and and_8 (and_8_out, d_ff_1_qn, out_5, out_6);
  and and_9 (and_9_out, d_ff_1_qn, d_ff_2_q, d_ff_3_q);
  or or_3 (out_8, and_8_out, and_9_out);

  assign out_9 = out_6;
endmodule
