// Logisim project datapath_GCD.circ as structural Verilog: 1 circuit, main circuit main
module main (
  input  [7:0] in_1,
  input  [7:0] inputY,
  input  lnx,
  input  lnY,
  input  xload,
  input  yload,
  input  clock,
  input  XY,
  input  out,
  output C1,
  output C2,
  output [7:0] \output 
);

  wire [7:0] multiplexer_1_out, multiplexer_2_out, multiplexer_3_out, multiplexer_4_out, register_1_q,
       register_2_q, subtractor_1_out;

  Multiplexer #(.width(8), .enable("false")) multiplexer_1 (
    .in0(in_1), .in1(subtractor_1_out), .out(multiplexer_1_out), .sel(lnx));
  Register register_1 (.D(multiplexer_1_out), .en(xload), .clk(clock), .Q(register_1_q));  // open: clr
  assign \output  = out ? register_1_q : 8'bz;  // Controlled_Buffer controlled_buffer_1
  Multiplexer #(.width(8), .enable("false")) multiplexer_2 (
    .in0(inputY), .in1(subtractor_1_out), .out(multiplexer_2_out), .sel(lnY));
  Register register_2 (.D(multiplexer_2_out), .en(yload), .clk(clock), .Q(register_2_q));  // open: clr
  Multiplexer #(.width(8), .enable("false")) multiplexer_3 (
    .in0(register_1_q), .in1(register_2_q), .out(multiplexer_3_out), .sel(XY));
  Multiplexer #(.width(8), .enable("false")) multiplexer_4 (
    .in0(register_2_q), .in1(register_1_q), .out(multiplexer_4_out), .sel(XY));
  Subtractor subtractor_1 (.a(multiplexer_3_out), .b(multiplexer_4_out), .out(subtractor_1_out));  // open: bin, bout
  Comparator comparator_1 (.a(register_2_q), .b(register_1_q), .gt(C1), .eq(C2));  // open: lt

  // Notes on the sheet:
  //   inputX
endmodule
